# Fritzing sketch Rasp_LEDs (saved by Fritzing 0.9.3b)
breadboards: 1

parts:
  LED1 = LED - 3mm [color="Blue (430nm)" package="3 mm [THT]"]
  LED2 = LED - 3mm [color="Red (633nm)" package="3 mm [THT]"]
  R1 = Resistor [tolerance=±5% resistance=220 package=THT]
  R2 = Resistor [tolerance=±5% resistance=220 package=THT]
  Raspberry_Pi_1 = Raspberry Pi 3 [part_number=RPI-3-V1.2]

nets:
  N1: LED1.cathode, LED2.cathode, Raspberry_Pi_1.GND
  N2: LED1.anode, R1.Pin_0
  N3: LED2.anode, R2.Pin_0
  N4: R1.Pin_1, Raspberry_Pi_1.GIPO23
  N5: R2.Pin_1, Raspberry_Pi_1.GIPO16

notes:
  Led Blue = GPIO23
  Led Red = GPIO16
