# Fritzing sketch Rasp_MAX6675 (saved by Fritzing 0.9.3b)

parts:
  Raspberry_Pi_1 = Raspberry Pi 3 [part_number=RPI-3-V1.2]
  U1 = MAX6675 [package=so08]

nets:
  3V3: Raspberry_Pi_1.3v3, U1.VDD
  N1: Raspberry_Pi_1.GPIO25, U1.SCK
  N2: Raspberry_Pi_1.GPIO24, U1.CS
  N3: Raspberry_Pi_1.GPIO18, U1.MISO
  GND: Raspberry_Pi_1.GND, U1.VSS

notes:
  CLK/SCK = 25
  CS = 24
  DO/SO/MISO = 18
  VCC = 3.3V
  GND = GND
