# Fritzing sketch Rasp_MAX6675_LED (saved by Fritzing 0.9.3b)
breadboards: 1

parts:
  Raspberry_Pi_1 = Raspberry Pi 3 [part_number=RPI-3-V1.2]
  U1 = MAX6675 [package=so08]
  LED1 = LED - 5mm [color="Blue (430nm)" package="5 mm [THT]"]
  R1 = Resistor [tolerance=±5% resistance=220 package=THT]

nets:
  3V3: Raspberry_Pi_1.3v3, U1.VDD
  N1: Raspberry_Pi_1.GPIO25, U1.SCK
  N2: Raspberry_Pi_1.GPIO24, U1.CS
  N3: Raspberry_Pi_1.GPIO18, U1.MISO
  N4: Raspberry_Pi_1.GPIO14, LED1.cathode
  GND: Raspberry_Pi_1.GND, U1.VSS
  N5: LED1.anode, R1.Pin_1

notes:
  CLK/SCK = 25
  CS = 24
  DO/SO/MISO = 18
  LED = 14
  VCC = 3.3V
  GND = GND
